// Logisim project CPU Design.circ as structural Verilog: 24 circuits, main circuit main
module main (
  input  reset,
  input  Reset_2
);

  wire clock_1_out, clock_2_out, control_unit_1_alusrc, control_unit_1_extsel, control_unit_1_memread,
       control_unit_1_memtoreg, control_unit_1_memwrite, control_unit_1_pc_src, control_unit_1_pcwrite,
       control_unit_1_regwrite;
  wire [2:0] control_unit_1_aluctrl;
  wire [5:0] alu_1_alu_out_2, extendunit_1_extimm_2;
  wire [11:0] alu_1_alu_out, extendunit_1_extimm, program_counter_1_pc_out;
  wire [17:0] data_memory_1_dataoutput, instruction_memory_1_out_2, multiplexer_1_out, register_file_1_p5,
       register_file_1_p7, register_file_1_p8;

  Program_Counter program_counter_1 (
    .PC_offset(extendunit_1_extimm), .PC_Write(control_unit_1_pcwrite), .reset(Reset_2),
    .PC_Src(control_unit_1_pc_src), .PC_Out(program_counter_1_pc_out));
  Instruction_Memory instruction_memory_1 (.PC_Address(program_counter_1_pc_out), .out_2(instruction_memory_1_out_2));
  Data_Memory data_memory_1 (
    .Address(alu_1_alu_out), .DataInput(register_file_1_p5), .WriteEnable(control_unit_1_memtoreg),
    .DataOutput(data_memory_1_dataoutput), .LoadEnable(control_unit_1_memread));
  Clock clock_1 (.out(clock_1_out));
  ExtendUnit extendunit_1 (
    .imm(instruction_memory_1_out_2[4:0]), .ExtSel(control_unit_1_extsel),
    .ExtImm({extendunit_1_extimm_2, extendunit_1_extimm}));
  Control_Unit control_unit_1 (
    .opcode(instruction_memory_1_out_2[4:0]), .clock(clock_1_out), .reset(reset),
    .RegWrite(control_unit_1_regwrite), .AluSrc(control_unit_1_alusrc), .MemRead(control_unit_1_memread),
    .MemToReg(control_unit_1_memtoreg), .PCWrite(control_unit_1_pcwrite), .ALUCtrl(control_unit_1_aluctrl),
    .PC_Src(control_unit_1_pc_src), .ExtSel(control_unit_1_extsel), .MemWrite(control_unit_1_memwrite));
  Clock clock_2 (.out(clock_2_out));
  ALU alu_1 (
    .input1(register_file_1_p5), .input2(multiplexer_1_out), .ALUctrl(control_unit_1_aluctrl),
    .ALU_out({alu_1_alu_out_2, alu_1_alu_out}));
  // Register_File register_file_1: pin names not known; wires that end beside it: clock_2_out, instruction_memory_1_out_2[4:1], instruction_memory_1_out_2[8:5], control_unit_1_regwrite, register_file_1_p5, instruction_memory_1_out_2[12:9], register_file_1_p7, register_file_1_p8
  Multiplexer #(.width(18)) multiplexer_1 (
    .in0(register_file_1_p7), .in1({extendunit_1_extimm_2, extendunit_1_extimm}), .out(multiplexer_1_out),
    .sel(control_unit_1_alusrc));  // open: en
  Multiplexer #(.width(18)) multiplexer_2 (
    .in0({alu_1_alu_out_2, alu_1_alu_out}), .in1(data_memory_1_dataoutput), .out(register_file_1_p8),
    .sel(control_unit_1_memwrite));  // open: en
endmodule

// DLatch
module D_Latch (
  input  D,
  input  C,
  output out_3
);

  wire and_1_out, and_2_out, nor_1_out;

  and and_1 (and_1_out, D, C);
  and and_2 (and_2_out, C, ~D);  // AND_Gate
  nor nor_1 (nor_1_out, and_1_out, out_3);
  nor nor_2 (out_3, nor_1_out, and_2_out);

  // Notes on the sheet:
  //   out_3: pull=up
endmodule

// DFF
module D_Flip_Flop (
  input  in_1,
  input  Clk,
  output Q
);

  wire d_latch_1_out_3, not_1_out;

  not not_1 (not_1_out, Clk);
  D_Latch d_latch_1 (.D(in_1), .C(not_1_out), .out_3(d_latch_1_out_3));
  D_Latch d_latch_2 (.D(d_latch_1_out_3), .C(Clk), .out_3(Q));
endmodule

module _4_bit_Register (
  input  [3:0] data_in,
  input  enable,
  input  reset,
  input  clock,
  output [3:0] data_out
);

  wire [3:0] multiplexer_1_out, multiplexer_2_out;

  Multiplexer #(.width(4), .enable("false")) multiplexer_1 (
    .in0(data_out), .in1(data_in), .out(multiplexer_1_out), .sel(enable));
  Multiplexer #(.width(4), .enable("false")) multiplexer_2 (
    .in0(multiplexer_1_out), .in1(4'b0000), .out(multiplexer_2_out), .sel(reset));
  D_Flip_Flop d_flip_flop_1 (.in_1(multiplexer_2_out[3]), .Clk(clock), .Q(data_out[3]));
  D_Flip_Flop d_flip_flop_2 (.in_1(multiplexer_2_out[2]), .Clk(clock), .Q(data_out[2]));
  D_Flip_Flop d_flip_flop_3 (.in_1(multiplexer_2_out[1]), .Clk(clock), .Q(data_out[1]));
  D_Flip_Flop d_flip_flop_4 (.in_1(multiplexer_2_out[0]), .Clk(clock), .Q(data_out[0]));
endmodule

// Register
module _12_bit_Register (
  input  [11:0] data_in,
  input  enable,
  input  reset,
  input  clock,
  output [11:0] data_out
);

  wire [11:0] multiplexer_1_out, multiplexer_2_out;

  Multiplexer #(.width(12), .enable("false")) multiplexer_1 (
    .in0(data_out), .in1(data_in), .out(multiplexer_1_out), .sel(enable));
  Multiplexer #(.width(12), .enable("false")) multiplexer_2 (
    .in0(multiplexer_1_out), .in1({12{1'b0}}), .out(multiplexer_2_out), .sel(reset));
  D_Flip_Flop d_flip_flop_1 (.in_1(multiplexer_2_out[11]), .Clk(clock), .Q(data_out[11]));
  D_Flip_Flop d_flip_flop_2 (.in_1(multiplexer_2_out[10]), .Clk(clock), .Q(data_out[10]));
  D_Flip_Flop d_flip_flop_3 (.in_1(multiplexer_2_out[9]), .Clk(clock), .Q(data_out[9]));
  D_Flip_Flop d_flip_flop_4 (.in_1(multiplexer_2_out[8]), .Clk(clock), .Q(data_out[8]));
  D_Flip_Flop d_flip_flop_5 (.in_1(multiplexer_2_out[7]), .Clk(clock), .Q(data_out[7]));
  D_Flip_Flop d_flip_flop_6 (.in_1(multiplexer_2_out[6]), .Clk(clock), .Q(data_out[6]));
  D_Flip_Flop d_flip_flop_7 (.in_1(multiplexer_2_out[5]), .Clk(clock), .Q(data_out[5]));
  D_Flip_Flop d_flip_flop_8 (.in_1(multiplexer_2_out[4]), .Clk(clock), .Q(data_out[4]));
  D_Flip_Flop d_flip_flop_9 (.in_1(multiplexer_2_out[3]), .Clk(clock), .Q(data_out[3]));
  D_Flip_Flop d_flip_flop_10 (.in_1(multiplexer_2_out[2]), .Clk(clock), .Q(data_out[2]));
  D_Flip_Flop d_flip_flop_11 (.in_1(multiplexer_2_out[1]), .Clk(clock), .Q(data_out[1]));
  D_Flip_Flop d_flip_flop_12 (.in_1(multiplexer_2_out[0]), .Clk(clock), .Q(data_out[0]));
endmodule

module _18_bit_Register (
  input  [17:0] data_in,
  input  enable,
  input  reset,
  input  clock,
  output [17:0] data_out
);

  wire [17:0] multiplexer_1_out, multiplexer_2_out;

  Multiplexer #(.width(18), .enable("false")) multiplexer_1 (
    .in0(data_out), .in1(data_in), .out(multiplexer_1_out), .sel(enable));
  Multiplexer #(.width(18), .enable("false")) multiplexer_2 (
    .in0(multiplexer_1_out), .in1({18{1'b0}}), .out(multiplexer_2_out), .sel(reset));
  D_Flip_Flop d_flip_flop_1 (.in_1(multiplexer_2_out[17]), .Clk(clock), .Q(data_out[17]));
  D_Flip_Flop d_flip_flop_2 (.in_1(multiplexer_2_out[16]), .Clk(clock), .Q(data_out[16]));
  D_Flip_Flop d_flip_flop_3 (.in_1(multiplexer_2_out[15]), .Clk(clock), .Q(data_out[15]));
  D_Flip_Flop d_flip_flop_4 (.in_1(multiplexer_2_out[14]), .Clk(clock), .Q(data_out[14]));
  D_Flip_Flop d_flip_flop_5 (.in_1(multiplexer_2_out[13]), .Clk(clock), .Q(data_out[13]));
  D_Flip_Flop d_flip_flop_6 (.in_1(multiplexer_2_out[12]), .Clk(clock), .Q(data_out[12]));
  D_Flip_Flop d_flip_flop_7 (.in_1(multiplexer_2_out[11]), .Clk(clock), .Q(data_out[11]));
  D_Flip_Flop d_flip_flop_8 (.in_1(multiplexer_2_out[10]), .Clk(clock), .Q(data_out[10]));
  D_Flip_Flop d_flip_flop_9 (.in_1(multiplexer_2_out[9]), .Clk(clock), .Q(data_out[9]));
  D_Flip_Flop d_flip_flop_10 (.in_1(multiplexer_2_out[8]), .Clk(clock), .Q(data_out[8]));
  D_Flip_Flop d_flip_flop_11 (.in_1(multiplexer_2_out[7]), .Clk(clock), .Q(data_out[7]));
  D_Flip_Flop d_flip_flop_12 (.in_1(multiplexer_2_out[6]), .Clk(clock), .Q(data_out[6]));
  D_Flip_Flop d_flip_flop_13 (.in_1(multiplexer_2_out[5]), .Clk(clock), .Q(data_out[5]));
  D_Flip_Flop d_flip_flop_14 (.in_1(multiplexer_2_out[4]), .Clk(clock), .Q(data_out[4]));
  D_Flip_Flop d_flip_flop_15 (.in_1(multiplexer_2_out[3]), .Clk(clock), .Q(data_out[3]));
  D_Flip_Flop d_flip_flop_16 (.in_1(multiplexer_2_out[2]), .Clk(clock), .Q(data_out[2]));
  D_Flip_Flop d_flip_flop_17 (.in_1(multiplexer_2_out[1]), .Clk(clock), .Q(data_out[1]));
  D_Flip_Flop d_flip_flop_18 (.in_1(multiplexer_2_out[0]), .Clk(clock), .Q(data_out[0]));
endmodule

module Half_Adder (
  input  a,
  input  b,
  output s,
  output co
);

  xor xor_1 (s, b, a);
  and and_1 (co, b, a);
endmodule

// Adder
module Full_Adder (
  input  A,
  input  B,
  input  Cin,
  output Sum,
  output Cout
);

  wire and_1_out, and_2_out, xor_1_out;

  xor xor_1 (xor_1_out, A, B);
  xor xor_2 (Sum, xor_1_out, Cin);
  and and_1 (and_1_out, xor_1_out, Cin);
  and and_2 (and_2_out, A, B);
  or or_1 (Cout, and_1_out, and_2_out);
endmodule

module _12_bit_Adder (
  input  Cin,
  input  [11:0] in_2,
  input  [11:0] in_3,
  output [11:0] out_4,
  output Cout
);

  wire full_adder_1_cout, full_adder_2_cout, full_adder_3_cout, full_adder_4_cout, full_adder_5_cout,
       full_adder_6_cout, full_adder_7_cout, full_adder_8_cout, full_adder_9_cout, full_adder_10_cout,
       full_adder_11_cout;

  Full_Adder full_adder_1 (.A(in_2[0]), .B(in_3[0]), .Cin(Cin), .Sum(out_4[0]), .Cout(full_adder_1_cout));
  Full_Adder full_adder_2 (.A(in_2[1]), .B(in_3[1]), .Cin(full_adder_1_cout), .Sum(out_4[1]), .Cout(full_adder_2_cout));
  Full_Adder full_adder_3 (.A(in_2[2]), .B(in_3[2]), .Cin(full_adder_2_cout), .Sum(out_4[2]), .Cout(full_adder_3_cout));
  Full_Adder full_adder_4 (.A(in_2[3]), .B(in_3[3]), .Cin(full_adder_3_cout), .Sum(out_4[3]), .Cout(full_adder_4_cout));
  Full_Adder full_adder_5 (.A(in_2[4]), .B(in_3[4]), .Cin(full_adder_4_cout), .Sum(out_4[4]), .Cout(full_adder_5_cout));
  Full_Adder full_adder_6 (.A(in_2[5]), .B(in_3[5]), .Cin(full_adder_5_cout), .Sum(out_4[5]), .Cout(full_adder_6_cout));
  Full_Adder full_adder_7 (.A(in_2[6]), .B(in_3[6]), .Cin(full_adder_6_cout), .Sum(out_4[6]), .Cout(full_adder_7_cout));
  Full_Adder full_adder_8 (.A(in_2[7]), .B(in_3[7]), .Cin(full_adder_7_cout), .Sum(out_4[7]), .Cout(full_adder_8_cout));
  Full_Adder full_adder_9 (.A(in_2[8]), .B(in_3[8]), .Cin(full_adder_8_cout), .Sum(out_4[8]), .Cout(full_adder_9_cout));
  Full_Adder full_adder_10 (
    .A(in_2[9]), .B(in_3[9]), .Cin(full_adder_9_cout), .Sum(out_4[9]), .Cout(full_adder_10_cout));
  Full_Adder full_adder_11 (
    .A(in_2[10]), .B(in_3[10]), .Cin(full_adder_10_cout), .Sum(out_4[10]), .Cout(full_adder_11_cout));
  Full_Adder full_adder_12 (.A(in_2[11]), .B(in_3[11]), .Cin(full_adder_11_cout), .Sum(out_4[11]), .Cout(Cout));
endmodule

// Adder
module _18_bit_Adder (
  input  Cin,
  input  [17:0] in_2,
  input  [17:0] in_3,
  output [17:0] out_4,
  output Cout
);

  wire full_adder_1_cout, full_adder_2_cout, full_adder_3_cout, full_adder_4_cout, full_adder_5_cout,
       full_adder_6_cout, full_adder_7_cout, full_adder_8_cout, full_adder_9_cout, full_adder_10_cout,
       full_adder_11_cout, full_adder_12_cout, full_adder_13_cout, full_adder_14_cout, full_adder_15_cout,
       full_adder_16_cout, full_adder_17_cout;

  Full_Adder full_adder_1 (.A(in_2[0]), .B(in_3[0]), .Cin(Cin), .Sum(out_4[0]), .Cout(full_adder_1_cout));
  Full_Adder full_adder_2 (.A(in_2[1]), .B(in_3[1]), .Cin(full_adder_1_cout), .Sum(out_4[1]), .Cout(full_adder_2_cout));
  Full_Adder full_adder_3 (.A(in_2[2]), .B(in_3[2]), .Cin(full_adder_2_cout), .Sum(out_4[2]), .Cout(full_adder_3_cout));
  Full_Adder full_adder_4 (.A(in_2[3]), .B(in_3[3]), .Cin(full_adder_3_cout), .Sum(out_4[3]), .Cout(full_adder_4_cout));
  Full_Adder full_adder_5 (.A(in_2[4]), .B(in_3[4]), .Cin(full_adder_4_cout), .Sum(out_4[4]), .Cout(full_adder_5_cout));
  Full_Adder full_adder_6 (.A(in_2[5]), .B(in_3[5]), .Cin(full_adder_5_cout), .Sum(out_4[5]), .Cout(full_adder_6_cout));
  Full_Adder full_adder_7 (.A(in_2[7]), .B(in_3[6]), .Cin(full_adder_6_cout), .Sum(out_4[6]), .Cout(full_adder_7_cout));
  Full_Adder full_adder_8 (.A(in_2[6]), .B(in_3[7]), .Cin(full_adder_7_cout), .Sum(out_4[7]), .Cout(full_adder_8_cout));
  Full_Adder full_adder_9 (.A(in_2[8]), .B(in_3[8]), .Cin(full_adder_8_cout), .Sum(out_4[8]), .Cout(full_adder_9_cout));
  Full_Adder full_adder_10 (
    .A(in_2[9]), .B(in_3[9]), .Cin(full_adder_9_cout), .Sum(out_4[9]), .Cout(full_adder_10_cout));
  Full_Adder full_adder_11 (
    .A(in_2[10]), .B(in_3[10]), .Cin(full_adder_10_cout), .Sum(out_4[10]), .Cout(full_adder_11_cout));
  Full_Adder full_adder_12 (
    .A(in_2[11]), .B(in_3[11]), .Cin(full_adder_11_cout), .Sum(out_4[11]), .Cout(full_adder_12_cout));
  Full_Adder full_adder_13 (
    .A(in_2[12]), .B(in_3[12]), .Cin(full_adder_12_cout), .Sum(out_4[12]), .Cout(full_adder_13_cout));
  Full_Adder full_adder_14 (
    .A(in_2[13]), .B(in_3[13]), .Cin(full_adder_13_cout), .Sum(out_4[13]), .Cout(full_adder_14_cout));
  Full_Adder full_adder_15 (
    .A(in_2[14]), .B(in_3[14]), .Cin(full_adder_14_cout), .Sum(out_4[14]), .Cout(full_adder_15_cout));
  Full_Adder full_adder_16 (
    .A(in_2[15]), .B(in_3[15]), .Cin(full_adder_15_cout), .Sum(out_4[15]), .Cout(full_adder_16_cout));
  Full_Adder full_adder_17 (
    .A(in_2[16]), .B(in_3[16]), .Cin(full_adder_16_cout), .Sum(out_4[16]), .Cout(full_adder_17_cout));
  Full_Adder full_adder_18 (.A(in_2[17]), .B(in_3[17]), .Cin(full_adder_17_cout), .Sum(out_4[17]), .Cout(Cout));
endmodule

// PC
module Program_Counter (
  input  [11:0] PC_offset,
  input  PC_Write,
  input  reset,
  input  PC_Src,
  output [11:0] PC_Out
);

  wire clock_1_out;
  wire [11:0] multiplexer_1_out, PC_1_out_4, PC_Offset_out_4;

  Multiplexer #(.width(12), .enable("false")) multiplexer_1 (
    .in0(PC_1_out_4), .in1(PC_Offset_out_4), .out(multiplexer_1_out), .sel(PC_Src));
  Clock clock_1 (.out(clock_1_out));
  _12_bit_Register u_12_bit_register_1 (
    .data_in(multiplexer_1_out), .enable(PC_Write), .reset(reset), .clock(clock_1_out), .data_out(PC_Out));
  _12_bit_Adder PC_1 (.Cin(1'b0), .in_2(PC_Out), .in_3(12'h1), .out_4(PC_1_out_4));  // open: Cout
  _12_bit_Adder u_PC_Offset (.Cin(1'b0), .in_2(PC_Out), .in_3(PC_offset), .out_4(PC_Offset_out_4));  // open: Cout
endmodule

// IM
module Instruction_Memory (
  input  [11:0] PC_Address,
  output [17:0] out_2
);

  ROM #(.addrWidth(12), .dataWidth(18)) rom_1 (.addr(PC_Address), .data(out_2));  // open: sel

  // Notes on the sheet:
  //   contents of rom_1 (hex, n*v repeats v):
  //   0 c62c 18a0c
endmodule

// RegisterFile
module Register_File (
  input  [17:0] WriteData,
  input  [3:0] rs1,
  input  [3:0] Write_Address,
  input  [3:0] rs2,
  input  Write_Enable,
  input  Reset,
  input  CLK,
  input  [3:0] ReadRegister2,
  input  [3:0] ReadRegister2_2,
  output [17:0] Output1,
  output [17:0] Output2
);

  wire and_1_out, and_2_out, and_3_out, and_4_out, and_5_out, and_6_out, and_7_out, and_8_out, and_9_out,
       and_10_out, and_11_out, and_12_out, and_13_out, and_14_out, and_15_out, and_16_out, decoder_1_out0,
       decoder_1_out1, decoder_1_out2, decoder_1_out3, decoder_1_out4, decoder_1_out5, decoder_1_out6,
       decoder_1_out7, decoder_1_out8, decoder_1_out9, decoder_1_out10, decoder_1_out11, decoder_1_out12,
       decoder_1_out13, decoder_1_out14, decoder_1_out15;
  wire [17:0] n18_bit_register_1_data_out, n18_bit_register_2_data_out, n18_bit_register_3_data_out,
       n18_bit_register_4_data_out, n18_bit_register_5_data_out, n18_bit_register_6_data_out,
       n18_bit_register_7_data_out, n18_bit_register_8_data_out, n18_bit_register_9_data_out,
       n18_bit_register_10_data_out, n18_bit_register_11_data_out, n18_bit_register_12_data_out,
       n18_bit_register_13_data_out, n18_bit_register_14_data_out, n18_bit_register_15_data_out,
       n18_bit_register_16_data_out;

  Decoder #(.select(4)) decoder_1 (
    .out0(decoder_1_out0), .out1(decoder_1_out1), .out2(decoder_1_out2), .out3(decoder_1_out3),
    .out4(decoder_1_out4), .out5(decoder_1_out5), .out6(decoder_1_out6), .out7(decoder_1_out7),
    .out8(decoder_1_out8), .out9(decoder_1_out9), .out10(decoder_1_out10), .out11(decoder_1_out11),
    .out12(decoder_1_out12), .out13(decoder_1_out13), .out14(decoder_1_out14), .out15(decoder_1_out15),
    .sel(Write_Address), .en(1'b1));
  and and_1 (and_1_out, decoder_1_out0, Write_Enable);
  and and_2 (and_2_out, decoder_1_out1, Write_Enable);
  and and_3 (and_3_out, decoder_1_out2, Write_Enable);
  and and_4 (and_4_out, decoder_1_out3, Write_Enable);
  and and_5 (and_5_out, decoder_1_out4, Write_Enable);
  and and_6 (and_6_out, decoder_1_out5, Write_Enable);
  and and_7 (and_7_out, decoder_1_out6, Write_Enable);
  and and_8 (and_8_out, decoder_1_out7, Write_Enable);
  and and_9 (and_9_out, decoder_1_out8, Write_Enable);
  and and_10 (and_10_out, decoder_1_out9, Write_Enable);
  and and_11 (and_11_out, decoder_1_out10, Write_Enable);
  and and_12 (and_12_out, decoder_1_out11, Write_Enable);
  and and_13 (and_13_out, decoder_1_out12, Write_Enable);
  and and_14 (and_14_out, decoder_1_out13, Write_Enable);
  and and_15 (and_15_out, decoder_1_out14, Write_Enable);
  and and_16 (and_16_out, decoder_1_out15, Write_Enable);
  _18_bit_Register u_18_bit_register_1 (
    .data_in(WriteData), .enable(and_1_out), .reset(Reset), .clock(CLK),
    .data_out(n18_bit_register_1_data_out));
  _18_bit_Register u_18_bit_register_2 (
    .data_in(WriteData), .enable(and_2_out), .reset(Reset), .clock(CLK),
    .data_out(n18_bit_register_2_data_out));
  _18_bit_Register u_18_bit_register_3 (
    .data_in(WriteData), .enable(and_3_out), .reset(Reset), .clock(CLK),
    .data_out(n18_bit_register_3_data_out));
  _18_bit_Register u_18_bit_register_4 (
    .data_in(WriteData), .enable(and_4_out), .reset(Reset), .clock(CLK),
    .data_out(n18_bit_register_4_data_out));
  _18_bit_Register u_18_bit_register_5 (
    .data_in(WriteData), .enable(and_5_out), .reset(Reset), .clock(CLK),
    .data_out(n18_bit_register_5_data_out));
  _18_bit_Register u_18_bit_register_6 (
    .data_in(WriteData), .enable(and_6_out), .reset(Reset), .clock(CLK),
    .data_out(n18_bit_register_6_data_out));
  _18_bit_Register u_18_bit_register_7 (
    .data_in(WriteData), .enable(and_7_out), .reset(Reset), .clock(CLK),
    .data_out(n18_bit_register_7_data_out));
  _18_bit_Register u_18_bit_register_8 (
    .data_in(WriteData), .enable(and_8_out), .reset(Reset), .clock(CLK),
    .data_out(n18_bit_register_8_data_out));
  _18_bit_Register u_18_bit_register_9 (
    .data_in(WriteData), .enable(and_9_out), .reset(Reset), .clock(CLK),
    .data_out(n18_bit_register_9_data_out));
  _18_bit_Register u_18_bit_register_10 (
    .data_in(WriteData), .enable(and_10_out), .reset(Reset), .clock(CLK),
    .data_out(n18_bit_register_10_data_out));
  _18_bit_Register u_18_bit_register_11 (
    .data_in(WriteData), .enable(and_11_out), .reset(Reset), .clock(CLK),
    .data_out(n18_bit_register_11_data_out));
  _18_bit_Register u_18_bit_register_12 (
    .data_in(WriteData), .enable(and_12_out), .reset(Reset), .clock(CLK),
    .data_out(n18_bit_register_12_data_out));
  _18_bit_Register u_18_bit_register_13 (
    .data_in(WriteData), .enable(and_13_out), .reset(Reset), .clock(CLK),
    .data_out(n18_bit_register_13_data_out));
  _18_bit_Register u_18_bit_register_14 (
    .data_in(WriteData), .enable(and_14_out), .reset(Reset), .clock(CLK),
    .data_out(n18_bit_register_14_data_out));
  _18_bit_Register u_18_bit_register_15 (
    .data_in(WriteData), .enable(and_15_out), .reset(Reset), .clock(CLK),
    .data_out(n18_bit_register_15_data_out));
  _18_bit_Register u_18_bit_register_16 (
    .data_in(WriteData), .enable(and_16_out), .reset(Reset), .clock(CLK),
    .data_out(n18_bit_register_16_data_out));
  Multiplexer #(.select(4), .width(18), .enable("false")) multiplexer_1 (
    .in0(n18_bit_register_1_data_out), .in1(n18_bit_register_2_data_out), .in2(n18_bit_register_3_data_out),
    .in3(n18_bit_register_4_data_out), .in4(n18_bit_register_5_data_out), .in5(n18_bit_register_6_data_out),
    .in6(n18_bit_register_7_data_out), .in7(n18_bit_register_8_data_out), .in8(n18_bit_register_9_data_out),
    .in9(n18_bit_register_10_data_out), .in10(n18_bit_register_11_data_out),
    .in11(n18_bit_register_12_data_out), .in12(n18_bit_register_13_data_out),
    .in13(n18_bit_register_14_data_out), .in14(n18_bit_register_15_data_out),
    .in15(n18_bit_register_16_data_out), .out(Output1), .sel(rs1));
  Multiplexer #(.select(4), .width(18), .enable("false")) multiplexer_2 (
    .in0(n18_bit_register_1_data_out), .in1(n18_bit_register_2_data_out), .in2(n18_bit_register_3_data_out),
    .in3(n18_bit_register_4_data_out), .in4(n18_bit_register_5_data_out), .in5(n18_bit_register_6_data_out),
    .in6(n18_bit_register_7_data_out), .in7(n18_bit_register_8_data_out), .in8(n18_bit_register_9_data_out),
    .in9(n18_bit_register_10_data_out), .in10(n18_bit_register_11_data_out),
    .in11(n18_bit_register_12_data_out), .in12(n18_bit_register_13_data_out),
    .in13(n18_bit_register_14_data_out), .in14(n18_bit_register_15_data_out),
    .in15(n18_bit_register_16_data_out), .out(Output2), .sel(rs2));
endmodule

module ALU (
  input  [17:0] input1,
  input  [17:0] input2,
  input  [2:0] ALUctrl,
  output [17:0] ALU_out
);

  wire [17:0] n18_bit_adder_1_out_4, n18_bit_adder_2_out_4, nand_1_out, nor_1_out, not_1_out,
       shifter_arithmetic_right_1_out_2, shifter_logical_right_1_out_2;

  assign not_1_out = ~input2;  // NOT_Gate not_1, 18 bits wide
  assign nand_1_out = ~(input1 & input2);  // NAND_Gate nand_1, 18 bits wide
  assign nor_1_out = ~(input1 | input2);  // NOR_Gate nor_1, 18 bits wide
  Shifter_Logical_Right shifter_logical_right_1 (.in_1(input2), .out_2(shifter_logical_right_1_out_2));
  Shifter_Arithmetic_Right shifter_arithmetic_right_1 (.in_1(input2), .out_2(shifter_arithmetic_right_1_out_2));
  _18_bit_Adder u_18_bit_adder_1 (
    .Cin(1'b0), .in_2(input1), .in_3(input2), .out_4(n18_bit_adder_1_out_4));  // open: Cout
  _18_bit_Adder u_18_bit_adder_2 (
    .Cin(1'b1), .in_2(input1), .in_3(not_1_out), .out_4(n18_bit_adder_2_out_4));  // open: Cout
  Multiplexer #(.select(3), .width(18), .enable("false")) multiplexer_1 (
    .in0(n18_bit_adder_1_out_4), .in1(n18_bit_adder_2_out_4), .in2(nand_1_out), .in3(nor_1_out),
    .in4(shifter_logical_right_1_out_2), .in5(shifter_arithmetic_right_1_out_2), .out(ALU_out), .sel(ALUctrl));  // open: in6, in7
endmodule

// Sign Ex
module Sign_Extend (
  input  [5:0] in_1,
  output [17:0] out_2
);

  Multiplexer #(.width(12), .enable("false")) multiplexer_1 (
    .in0({12{1'b0}}), .in1({12{1'b1}}), .out(out_2[17:6]), .sel(in_1[5]));

  assign out_2[5:0] = in_1;
endmodule

module _5_18_bit_Sign_Extend (
  input  [4:0] in,
  output [17:0] extended_out
);

  and and_1 (extended_out[17], in[4], in[4]);

  assign extended_out[16:0] = {{13{extended_out[17]}}, in[3:0]};
endmodule

module Sign_Extend_13_18_Bit (
  input  [12:0] in_1,
  output [17:0] out_2
);

  Multiplexer #(.width(5), .enable("false")) multiplexer_1 (
    .in0({5{1'b0}}), .in1({5{1'b1}}), .out(out_2[17:13]), .sel(in_1[12]));

  assign out_2[12:0] = in_1;
endmodule

// Zero Ex
module Zero_Extend (
  input  [8:0] in,
  output [11:0] extended_out
);


  assign extended_out = {3'b000, in};
endmodule

module _5_18_bit_Zero_Extend (
  input  [4:0] in,
  output [17:0] extended_out
);


  assign extended_out = {{13{1'b0}}, in};
endmodule

// Extend
module ExtendUnit (
  input  [4:0] imm,
  input  ExtSel,
  output [17:0] ExtImm
);

  wire [17:0] bit_extender_1_out, n5_18_bit_sign_extend_1_extended_out;

  assign bit_extender_1_out = {{13{1'b0}}, imm};  // Bit_Extender bit_extender_1
  _5_18_bit_Sign_Extend u_5_18_bit_sign_extend_1 (.in(imm), .extended_out(n5_18_bit_sign_extend_1_extended_out));
  Multiplexer #(.width(18), .enable("false")) multiplexer_1 (
    .in0(bit_extender_1_out), .in1(n5_18_bit_sign_extend_1_extended_out), .out(ExtImm), .sel(ExtSel));
endmodule

module Shifter_Logical_Right (
  input  [17:0] in_1,
  output [17:0] out_2
);


  assign out_2 = {1'b0, in_1[17:1]};
endmodule

module Shifter_Arithmetic_Right (
  input  [17:0] in_1,
  output [17:0] out_2
);


  assign out_2 = {{2{in_1[17]}}, in_1[16:1]};
endmodule

// Memory
module Data_Memory (
  input  [11:0] Address,
  input  [17:0] DataInput,
  input  WriteEnable,
  input  LoadEnable,
  output [17:0] DataOutput
);

  wire clock_1_out;

  Clock clock_1 (.out(clock_1_out));
  RAM #(.addrWidth(12), .dataWidth(18), .bus("separate")) ram_1 (
    .addr(Address), .din(DataInput), .data(DataOutput), .str(WriteEnable), .sel(1'b1), .clk(clock_1_out),
    .ld(LoadEnable), .clr(1'b0));
endmodule

// CU
module Control_Unit (
  input  [4:0] opcode,
  input  clock,
  input  reset,
  output RegWrite,
  output AluSrc,
  output MemRead,
  output MemToReg,
  output PCWrite,
  output [2:0] ALUCtrl,
  output PC_Src,
  output ExtSel,
  output MemWrite
);

  wire and_3_out, and_5_out, and_6_out, and_7_out, and_8_out, decoder_1_out0, decoder_1_out1, decoder_1_out2,
       decoder_1_out3, decoder_1_out4, decoder_1_out5, decoder_1_out6, decoder_1_out7, decoder_1_out8,
       decoder_1_out9, decoder_1_out10, decoder_1_out11, decoder_1_out12, decoder_1_out13, decoder_1_out16,
       decoder_2_out0, decoder_2_out3, decoder_2_out4, decoder_2_out5, decoder_2_out6, isItype_out, or_4_out;
  wire [3:0] StateReg_data_out;

  Decoder #(.select(5)) decoder_1 (
    .out0(decoder_1_out0), .out1(decoder_1_out1), .out2(decoder_1_out2), .out3(decoder_1_out3),
    .out4(decoder_1_out4), .out5(decoder_1_out5), .out6(decoder_1_out6), .out7(decoder_1_out7),
    .out8(decoder_1_out8), .out9(decoder_1_out9), .out10(decoder_1_out10), .out11(decoder_1_out11),
    .out12(decoder_1_out12), .out13(decoder_1_out13), .out16(decoder_1_out16), .sel(opcode));  // open: out14, out15, out17, out18, out19, out20, out21, out22, out23, out24, out25, out26, out27, out28, out29, out30, out31, en
  _4_bit_Register StateReg (.reset(reset), .clock(clock), .data_out(StateReg_data_out));  // open: data_in, enable
  Decoder #(.select(4)) decoder_2 (
    .out0(decoder_2_out0), .out3(decoder_2_out3), .out4(decoder_2_out4), .out5(decoder_2_out5),
    .out6(decoder_2_out6), .sel(StateReg_data_out));  // open: out1, out2, out7, out8, out9, out10, out11, out12, out13, out14, out15, en
  or isJump (PC_Src, decoder_1_out10, decoder_1_out11);
  or Ctrl0 (ALUCtrl[0], decoder_1_out4, decoder_1_out5);
  or Ctrl1 (ALUCtrl[1], decoder_1_out2, decoder_1_out3, decoder_1_out8, decoder_1_out9);
  or Ctrl0_2 (ALUCtrl[2], decoder_1_out1, decoder_1_out3, decoder_1_out5, decoder_1_out7, decoder_1_out9);
  or isItype (isItype_out, decoder_1_out6, decoder_1_out7, decoder_1_out8, decoder_1_out9);
  and and_1 (MemRead, decoder_2_out5, decoder_1_out12);
  and and_2 (MemWrite, decoder_2_out5, decoder_1_out13);
  and and_3 (and_3_out, decoder_2_out3, PC_Src);
  or or_1 (AluSrc, isItype_out, decoder_1_out12, decoder_1_out13, decoder_1_out16);
  or or_2 (ExtSel, decoder_1_out12, decoder_1_out13, decoder_1_out7, decoder_1_out6);
  and and_4 (MemToReg, decoder_2_out6, decoder_1_out13);
  or or_3 (PCWrite, decoder_2_out0, and_3_out);
  or or_4 (or_4_out, decoder_1_out0, decoder_1_out1, decoder_1_out2, decoder_1_out3, decoder_1_out4, decoder_1_out5, decoder_1_out16);
  and and_5 (and_5_out, decoder_2_out4, isItype_out);
  and and_6 (and_6_out, decoder_2_out4, decoder_1_out11);
  and and_7 (and_7_out, decoder_2_out4, decoder_1_out12);
  and and_8 (and_8_out, or_4_out, decoder_2_out4);
  or or_5 (RegWrite, and_8_out, and_5_out, and_6_out, and_7_out);
endmodule
